# Fritzing sketch datalogger-amplificador_instrumentacion-termocupla-atmega328p_v1.2 (saved by Fritzing 1.0.1rc)
circuit board: 4cm x 10cm
circuit board: 15cm x 10cm

parts:
  reset = Pushbutton [package="[THT]"]
  Cristal = Crystal [frequency="16 Mhz" package=THT]
  D2 = Header 1 [package=1x01_offset]
  D3 = Header 1 [package=1x01_offset]
  D4 = Header 1 [package=1x01_offset]
  D5 = Header 1 [package=1x01_offset]
  D7 = Header 1 [package=1x01_offset]
  D6 = Header 1 [package=1x01_offset]
  ARef = Header 1 [package=1x01_offset]
  GND = Header 1 [package=1x01_offset]
  GND_2 = Header 1 [package=1x01_offset]
  C3 = Capacitor [package=cap-pth-5mm]
  C2 = Capacitor [package=cap-pth-5mm]
  reset_2 = Header 1 [package=1x01_offset]
  reset_3 = Header 1 [package=1x01_offset]
  D8 = Header 1 [package=1x01_offset]
  Atmega328p = atmega328 [package=dip]
  U4 = LM 358 Dual Op-Amp [package="DIP8 [THT]"]
  U5 = LM 358 Dual Op-Amp [package="DIP8 [THT]"]
  D17 = Zener Diode [part_number=1N4732A breakdown_voltage=3.6V package="300 mil [THT]"]
  9V = Header 1 [package=1x01_offset]
  GND_3 = Header 1 [package=1x01_offset]
  GND_4 = Header 1 [package=1x01_offset]
  R20 = Header 1 [package=1x01_offset]
  R20_2 = Header 1 [package=1x01_offset]
  A3 = Header 1 [package=1x01_offset]
  R22 = Resistor [tolerance=±1% resistance=1k power=0.25 package=THT]
  R23 = Resistor [tolerance=±1% resistance=1k power=0.25 package=THT]
  R24 = Resistor [tolerance=±1% resistance=1k power=0.25 package=THT]
  R25 = Resistor [tolerance=±1% resistance=1k power=0.25 package=THT]
  R26 = Resistor [tolerance=±1% resistance=1k power=0.25 package=THT]
  R27 = Resistor [tolerance=±1% resistance=3.3k power=0.25 package=THT]
  R28 = Resistor [tolerance=±1% resistance=3.3k power=0.25 package=THT]
  R29 = Resistor [tolerance=±1% resistance=1k power=0.25 package=THT]
  R30 = Resistor [tolerance=±1% resistance=1k power=0.25 package=THT]
  R31 = Resistor [tolerance=±1% resistance=100k power=0.25 package=THT]
  R32 = Resistor [tolerance=±1% resistance=100k power=0.25 package=THT]
  R33 = Resistor [tolerance=±5% resistance=100k power=0.25 package=THT]
  R34 = Resistor [tolerance=±1% resistance=100k power=0.25 package=THT]
  R35 = Resistor [tolerance=±1% resistance=1k power=0.25 package=THT]
  SD = MicroSD Card Module
  R36 = Resistor [tolerance=±5% resistance=2.2k power=0.25 package=THT]
  GND_5 = Header 1 [package=1x01_offset]
  VCC = Header 1 [package=1x01_offset]
  -9V = Header 1 [package=1x01_offset]
  -9V_2 = Header 1 [package=1x01_offset]
  Part1 = Analog Digital MUX Breakout
  CH0 = screw terminal, 16 pins
  DS18B20 = Header 1 [package=1x01_offset]
  CH1 = screw terminal, 12 pins
  A3_2 = Header 1 [package=1x01_offset]
  D7_2 = Header 1 [package=1x01_offset]
  D6_2 = Header 1 [package=1x01_offset]
  D5_2 = Header 1 [package=1x01_offset]
  D18 = Rectifier Diode [part_number=1N4001 package="300 mil [THT]"]
  D20 = Rectifier Diode [part_number=1N4001 package="300 mil [THT]"]
  D21 = Rectifier Diode [part_number=1N4001 package="300 mil [THT]"]
  D22 = Rectifier Diode [part_number=1N4001 package="300 mil [THT]"]
  C7 = Ceramic Capacitor [capacitance=100nF package="100 mil [THT, multilayer]"]
  7809 = Voltage Regulator [package=to220-igo]
  7909 = Voltage Regulator [package=to220-igo]
  C10 = Ceramic Capacitor [capacitance=100nF package="100 mil [THT, multilayer]"]
  C11 = Ceramic Capacitor [capacitance=100nF package="100 mil [THT, multilayer]"]
  C12 = Electrolytic Capacitor [capacitance=22µF voltage=35V package="100 mil [THT, electrolytic]"]
  C13 = Ceramic Capacitor [capacitance=100nF package="100 mil [THT, multilayer]"]
  7805 = Voltage Regulator [package=to220-igo]
  C14 = Electrolytic Capacitor [capacitance=22µF voltage=35V package="100 mil [THT, electrolytic]"]
  C15 = Ceramic Capacitor [capacitance=100nF package="100 mil [THT, multilayer]"]
  7803 = Voltage Regulator [package=to220-igo]
  VCC_2 = Header 1 [package=1x01_offset]
  JP1 = Header 1 [package=1x01_offset]
  JP2 = Header 1 [package=1x01_offset]
  JP3 = Header 1 [package=1x01_offset]
  JP4 = Header 1 [package=1x01_offset]
  JP5 = Header 1 [package=1x01_offset]
  D8_2 = Header 1 [package=1x01_offset]
  D10 = Header 1 [package=1x01_offset]
  9V_2 = Header 1 [package=1x01_offset]
  Salida = screw terminal, 5 pins
  Entrada = screw terminal, 5 pins
  C5 = Electrolytic Capacitor [capacitance=22µF voltage=35V package="300 mil [THT, electrolytic]"]
  TRAFO = screw terminal, 3 pins
  VCC_3 = Header 1 [package=1x01_offset]
  VCC_4 = Header 1 [package=1x01_offset]
  C4 = Electrolytic Capacitor [capacitance=22µF voltage=35V package="300 mil [THT, electrolytic]"]
  C6 = Ceramic Capacitor [capacitance=100nF package="100 mil [THT, multilayer]"]
  9V_3 = Header 1 [package=1x01_offset]
  9V_4 = Header 1 [package=1x01_offset]
  C8 = Electrolytic Capacitor [capacitance=22µF voltage=35V package="200 mil [THT, electrolytic]"]
  C9 = Electrolytic Capacitor [capacitance=22µF voltage=35V package="200 mil [THT, electrolytic]"]
  9V_5 = Header 1 [package=1x01_offset]
  D10_2 = Header 1 [package=1x01_offset]
  U6 = POT [knob_status=50% package=trim_pot]
  R37 = Resistor [tolerance=±5% resistance=1M power=0.25 package=THT]
  L1 = Inductor [inductance=10µH package="400 mil [THT]"]
  C104 = Capacitor [package=cap-pth-5mm]
  C104_2 = Capacitor [package=cap-pth-5mm]
  VCC_5 = Header 1 [package=1x01_offset]
  VCC_6 = Header 1 [package=1x01_offset]
  ZS-042_RTC1 = ZS-042 RTC Module

nets (from the pcb view):
  GND: reset.Pin_1, reset.Pin_2, GND.1, GND_2.1, C3.1, C2.1, Atmega328p.GND, U5.connector4, D17.anode, GND_3.1, GND_4.1, R24.Pin_0, R28.Pin_0, SD.GND, GND_5.1, Part1.GND, Part1.EN, CH0.pin4, CH0.pin8, CH0.pin12, CH0.pin16, CH1.pin4, CH1.pin8, CH1.pin10, CH1.pin12, Entrada.pin2, U6.A, C104.2, C104_2.2, ZS-042_RTC1.GND
  N1: reset.Pin_4, reset_2.1, reset_3.1, Atmega328p.RESET
  N2: Cristal.pin_0, C3.2, Atmega328p.XLAT2, R37.Pin_0
  N3: Cristal.pin_1, C2.2, Atmega328p.XLAT1, R37.Pin_1
  N4: D2.1, Atmega328p.D2
  N5: D3.1, Atmega328p.D3_(PWM)
  N6: D4.1, Atmega328p.D4
  N7: D5.1, Atmega328p.D5_(PWM), Part1.S3, D5_2.1
  N8: D7.1, Atmega328p.D7, Part1.S1, D7_2.1
  N9: D6.1, Atmega328p.D6_(PWM), Part1.S2, D6_2.1
  N10: ARef.1, Atmega328p.AREF, R26.Pin_1, Entrada.pin5
  N11: D8.1, Atmega328p.D8, Part1.S0, D8_2.1
  VCC: Atmega328p.VCC, SD.VCC, R36.Pin_1, VCC.1, Part1.VCC, VCC_2.1, Entrada.pin4, VCC_3.1, VCC_4.1, L1.pin_1, C104_2.1, VCC_5.1, VCC_6.1, ZS-042_RTC1.VCC
  N12: Atmega328p.D9_(PWM), SD.CS
  N13: Atmega328p.D10_(PWM), R36.Pin_0, CH0.pin3, CH0.pin7, CH0.pin11, CH0.pin15, DS18B20.1, CH1.pin3, CH1.pin7, CH1.pin9, CH1.pin11, JP1.1, JP2.1, JP3.1, JP4.1, JP5.1, D10.1, D10_2.1
  N14: Atmega328p.D11_(PWM), SD.MOSI
  N15: Atmega328p.D12, SD.MISO
  N16: Atmega328p.D13, SD.SCK
  N17: Atmega328p.AVCC, L1.pin_0, C104.1
  N18: Atmega328p.A3, U4.connector6, D17.cathode, A3.1, R23.Pin_1, A3_2.1
  N19: Atmega328p.A4, ZS-042_RTC1.SDA
  N20: Atmega328p.A5, ZS-042_RTC1.SCL
  N21: U4.connector0, R25.Pin_0, R27.Pin_1
  N22: U4.connector1, R27.Pin_0, R29.Pin_1
  N23: U4.connector2, R28.Pin_1, R30.Pin_1
  N24: U4.connector3, U5.connector3, -9V.1, -9V_2.1, Entrada.pin3
  N25: U4.connector4, R24.Pin_1, R25.Pin_1
  N26: U4.connector5, R22.Pin_1, R23.Pin_0
  N27: U4.connector7, U5.connector7, 9V.1, 9V_2.1, Entrada.pin1, 9V_5.1
  N28: U5.connector0, R29.Pin_0, R33.Pin_1
  N29: U5.connector1, R34.Pin_0, R35.Pin_1
  N30: U5.connector2, Part1.SIG
  N31: U5.connector5, R20.1, R20_2.1, R32.Pin_0, R35.Pin_0
  N32: U5.connector6, R30.Pin_0, R31.Pin_1
  N33: R22.Pin_0, U6.S
  N34: R26.Pin_0, U6.E
  N35: R31.Pin_0, R32.Pin_1
  N36: R33.Pin_0, R34.Pin_1
  N37: Part1.C0, CH0.pin1
  N38: Part1.C1, CH0.pin2
  N39: Part1.C2, CH0.pin5
  N40: Part1.C3, CH0.pin6
  N41: Part1.C4, CH0.pin9
  N42: Part1.C5, CH0.pin10
  N43: Part1.C6, CH0.pin13
  N44: Part1.C7, CH0.pin14
  N45: Part1.C8, CH1.pin1
  N46: Part1.C9, CH1.pin2
  N47: Part1.C10, CH1.pin5
  N48: Part1.C11, CH1.pin6
  N49: D18.cathode, D20.cathode, 7809.IN, C4.+, C6.1
  N50: D18.anode, D21.cathode, TRAFO.pin3
  N51: D20.anode, D22.cathode, TRAFO.pin1
  N52: D21.anode, D22.anode, C7.0, 7909.IN, C5.-
  GND_2: C7.1, 7809.GND, 7909.GND, C10.1, C11.0, C12.-, C13.0, 7805.GND, C14.-, C15.0, 7803.GND, Salida.pin2, C5.+, TRAFO.pin2, C4.-, C6.0, C8.+, C9.-
  N53: 7809.OUT, C11.1, 7805.IN, Salida.pin1, 9V_3.1, 9V_4.1, C9.+
  N54: 7909.OUT, C10.0, Salida.pin3, C8.-
  N55: C12.+, C13.1, 7805.OUT, 7803.IN, Salida.pin4
  N56: C14.+, C15.1, 7803.OUT, Salida.pin5

notes:
  Etapa de energizacion
  Etapa Arduino
  Medicion
  divisor tension ajuste offset
  Amplificador de Instrumentación
  termo (-)
  termo (+)
  Registro de tiempo
  Almacenamiento/memoria SD
  sensor DS18B20
  Multiplexor
  GND
  9V
  -9V
  5V
  3.3V

// code stored in the sketch: PaperduinoPCB+lcd+Nati-v1.1.ino
// Fecha 14/08/2019
//  _ ___ _______     ___ ___ ___  ___ _   _ ___ _____ ___ 
// / |_  )__ /   \   / __|_ _| _ \/ __| | | |_ _|_   _/ __| 
// | |/ / |_ \ |) | | (__ | ||   / (__| |_| || |  | | \__ \ 
// |_/___|___/___/   \___|___|_|_\\___|\___/|___| |_| |___/ 
// 
// Glow Wire Apparatus
// 
// Made by lpeisino lpeisino
// License: CC-BY-SA 3.0

// Programa para corren en Arduino UNO - Atmega328 - SIN CONEXION A LA PC
// sensor de temp LM35 con referencia interna para aumentar la resolucion 
// y estabilizacion de la senal mediante in filtro digital IIF

#include <EEPROM.h> // libreria para poder escribir en la memoria del atmega328
#include <LiquidCrystal.h> // include the library code
#include "DHT.h" // libreria para leer datos de los sensores de humedad y temperatura DHT11 y DHT22

#define DHTPINuno 9     // Pin donde está conectado el sensor1
#define DHTPINdos 11     // Pin donde está conectado el sensor1


//#define DHTTYPE DHT11   // Descomentar si se usa el DHT 11
#define DHTTYPE DHT22   // Sensor DHT22

DHT dht1(DHTPINuno, DHTTYPE);
DHT dht2(DHTPINdos, DHTTYPE);

int c=0;
//varialbles del filtro pasa bajos
float Hy1,Hyant1=0,Hxant1=0;
float Ty1,Tyant1=0,Txant1=0;
float Hy2,Hyant2=0,Hxant2=0;
float Ty2,Tyant2=0,Txant2=0;

int relay = 12;

int settempU = EEPROM.read (1);
int settempD = EEPROM.read (2);
int settempC = EEPROM.read (3);
float settemp = (settempC*100) + (settempD*10) + settempU;
//float settemp = 0;
LiquidCrystal lcd(3, 4 ,5 ,6 ,7 ,8); // lcd is at 7,9,10,11,12,13

byte grado[8]={
  0b00111,
  0b00101,
  0b00111,
  0b00000,          //para asignar los valores del simbolo °C
  0b00000,
  0b00000,
  0b00000,
  0b00000
};


void setup() {
  Serial.begin(9600);
  Serial.println("Iniciando...");
  dht1.begin(); //inicio de Sensor1
  dht2.begin(); //inicio de Sensor2
  pinMode(relay, OUTPUT);
}
void loop() {
  int span = 20;

  //Lectura del Sensor1
  float h1 = 0 ; //dht1.readHumidity(); //Leemos la Humedad
  float t1 = 0 ; //dht1.readTemperature(); //Leemos la temperatura en grados Celsius  
    for (int i = 0; i < span; i++) {
	delay(2500);        
	h1 = h1 + dht1.readHumidity(); //Leemos la Humedad
        t1 = t1 + dht1.readTemperature(); //Leemos la temperatura en grados Celsius  
        }
  
  h1 = h1 / 20;
  t1 = t1 / 20;
  
  //Lectura del Sensor1
  float h2 = 0 ; //dht2.readHumidity(); //Leemos la Humedad
  float t2 = 0 ; //dht2.readTemperature(); //Leemos la temperatura en grados Celsius  
    for (int i = 0; i < span; i++) {
        delay(2500);
        h2 = h2 + dht2.readHumidity(); //Leemos la Humedad
        t2 = t2 + dht2.readTemperature(); //Leemos la temperatura en grados Celsius  
        }
  
  h2 = h2 / 20;
  t2 = t2 / 20;

  //Calibracion para humedad del sensor1
  float Auno = 0.91854;
  float Buno = 12.28375;
  
  float hh1 = Auno*h1 + Buno;
  
  //Calibracion para humedad del sensor2
  float Ados = 0.85567;
  float Bdos = 14.11819;
  
  float hh2 = Ados*h2 + Bdos;

if (c==0) {Hyant1=hh1;
           Hxant1=hh1;
          
           Tyant1=t1;
           Txant1=t1;
           
           Hyant2=hh2;
           Hxant2=hh2;
           
           Tyant2=t2;
           Txant2=t2;
           }
  c=1;

//Aplicacion del filtro pasa bajos para las magnitudes de humedad y temperatura
  Hy1=0.6859*Hyant1+0.3141*Hxant1;
  Hyant1=Hy1;
  Hxant1=hh1;

  Ty1=0.6859*Tyant1+0.3141*Txant1;
  Tyant1=Ty1;
  Txant1=t1;
  
  Hy2=0.6859*Hyant2+0.3141*Hxant2;
  Hyant2=Hy2;
  Hxant2=hh2;
  
  Ty2=0.6859*Tyant2+0.3141*Txant2;
  Tyant2=Ty2;
  Txant2=t2;


  //--------Enviamos las lecturas por el puerto serial-------------
  Serial.print("Humedad ");
  //Serial.print(h);
  Serial.print("\t");
  Serial.print(Hy1,2);
  Serial.print("\t");
  Serial.print(Hy2,2);
  Serial.print("\t");
  Serial.print("Temperatura: ");
  Serial.print(Ty1,1);
  Serial.print(" *C ");
  Serial.print("\t");
  Serial.print(Ty2,1);
  Serial.println(" *C ");

//encendido y apagado del relay
if (Hy1 < 80) {
            digitalWrite(relay, HIGH);   // si la humedad es menos que 70% encender el relay
           } else { 
            digitalWrite(relay, LOW);
           }

  delay(2000);
  }
